# Fritzing sketch co2monitor v1.12 (saved by Fritzing 0.9.3b)
stripboards: 1

parts:
  C2 = Electrolytic Capacitor [capacitance=0.1mF package="100 mil [THT, electrolytic]"]
  ESPDEVKITV1_RHS1 = ESP32 DEVKITV1 RHS - 15 pins [form="♀ (female)" package=THT]
  LED3 = smd LED [color="Red (635nm)" package="0603 [SMD]"]  # not connected
  LED4 = smd LED [color="Green (555nm)" package="0603 [SMD]"]  # not connected
  DHT23 = Humidity and Temperature Sensor RHT03
  ESPDEVKITV1_LHS1 = ESP32 DEVKITV1 LHS - 15 pins [form="♀ (female)" package=THT]
  C3 = Electrolytic Capacitor [capacitance=10µF package="100 mil [THT, electrolytic]"]
  RED_LED_Header = LED Female Header [form="♀ (female)" package=THT]
  Green_LED_Header = LED Female Header [form="♀ (female)" package=THT]
  J3 = female pin header, 5 pins [form="♀ (female)"]
  co2_sensor = female pin header, 4 pins [form="♀ (female)"]
  LED5 = smd LED [color="Yellow (595nm)" package="0603 [SMD]"]  # not connected
  r1 = Resistor [tolerance=±5% resistance=220 package=THT]
  r2 = Resistor [tolerance=±5% resistance=220 package=THT]
  r3 = Resistor [tolerance=±5% resistance=220 package=THT]
  YellowLED_Header1 = LED Female Header [form="♀ (female)" package=THT]
  J2 = male pin header, 3 pins [form="♂ (male)"]
  J4 = female pin header, 3 pins [form="♀ (female)"]
  r4 = Resistor [tolerance=±5% resistance=10k package=THT]
  Grove1 = Grove OLED 128x96  # not connected

nets:
  GND: C2.-, ESPDEVKITV1_RHS1.GND, ESPDEVKITV1_LHS1.GND, C3.-, RED_LED_Header.-ve, Green_LED_Header.-ve, co2_sensor.pin2, YellowLED_Header1.-ve, J4.pin3
  3.3V: C2.+, ESPDEVKITV1_RHS1.VDD_3V3, J4.pin1, r4.Pin_0
  N1: ESPDEVKITV1_RHS1.GPIO16, J3.pin3
  N2: ESPDEVKITV1_RHS1.GPIO17, J3.pin2
  N3: DHT23.Vcc, J2.pin1
  N4: DHT23.Data-signal, J2.pin2
  N5: DHT23.GND_1, J2.pin3
  5V: ESPDEVKITV1_LHS1.VIN, C3.+, co2_sensor.pin1
  N6: ESPDEVKITV1_LHS1.GPIO13, r1.Pin_0
  N7: ESPDEVKITV1_LHS1.GPIO12, r2.Pin_0
  N8: ESPDEVKITV1_LHS1.GPIO14, r3.Pin_0
  N9: ESPDEVKITV1_LHS1.GPIO25, J4.pin2, r4.Pin_1
  N10: RED_LED_Header.+ve, r1.Pin_1
  N11: Green_LED_Header.+ve, r2.Pin_1
  N12: r3.Pin_1, YellowLED_Header1.+ve

notes:
  Note that GPIO_NUM_34 – GPIO_NUM_39 are input mode only
