# Fritzing sketch co2monitor v1.22 make with oled pullups (saved by Fritzing 0.9.3b)
stripboards: 1

parts:
  C2 = Electrolytic Capacitor [capacitance=0.1mF package="100 mil [THT, electrolytic]"]
  ESPDEVKITV1_RHS1 = ESP32 DEVKITV1 RHS - 15 pins [form="♀ (female)" package=THT]
  LED3 = smd LED [color="Red (635nm)" package="0603 [SMD]"]  # not connected
  LED4 = smd LED [color="Green (555nm)" package="0603 [SMD]"]  # not connected
  DHT23 = Humidity and Temperature Sensor RHT03
  ESPDEVKITV1_LHS1 = ESP32 DEVKITV1 LHS - 15 pins [form="♀ (female)" package=THT]
  C3 = Electrolytic Capacitor [capacitance=10µF package="100 mil [THT, electrolytic]"]
  green = LED Female Header [form="♀ (female)" package=THT]
  yellow = LED Female Header [form="♀ (female)" package=THT]
  co2_sensor = female pin header, 4 pins [form="♀ (female)"]
  LED5 = smd LED [color="Yellow (595nm)" package="0603 [SMD]"]  # not connected
  r1 = Resistor [tolerance=±5% resistance=100 package=THT]
  r2 = Resistor [tolerance=±5% resistance=100 package=THT]
  r3 = Resistor [tolerance=±5% resistance=100 package=THT]
  red = LED Female Header [form="♀ (female)" package=THT]
  J2 = male pin header, 3 pins [form="♂ (male)"]
  dht_skt = female pin header, 3 pins [form="♀ (female)"]
  r4 = Resistor [tolerance=±5% resistance=10k package=THT]
  OLED = Grove OLED 128x96
  oled_skt = female pin header, 4 pins [form="♀ (female)"]
  keypad = female pin header, 3 pins [form="♀ (female)"]
  J3 = Piezo Speaker
  keypad_plg = male pin header, 3 pins [form="♂ (male)"]  # not connected
  OLED_plg = male pin header, 4 pins [form="♂ (male)"]
  sounder_plg = male pin header, 2 pins [form="♂ (male)"]
  sounder = female pin header, 2 pins [form="♀ (female)"]
  co2_sensor_plg = male pin header, 4 pins [form="♂ (male)"]  # not connected
  r5 = Resistor [tolerance=±5% resistance=4.7k package=THT]
  r6 = Resistor [tolerance=±5% resistance=4.7k package=THT]
  switch1 = female pin header, 2 pins [form="♀ (female)"]
  switch2 = female pin header, 2 pins [form="♀ (female)"]

nets:
  GND: C2.-, ESPDEVKITV1_RHS1.GND, ESPDEVKITV1_LHS1.GND, C3.-, green.-ve, yellow.-ve, co2_sensor.pin4, red.-ve, dht_skt.pin3, oled_skt.pin4, keypad.pin3, sounder.pin2
  3.3V: C2.+, ESPDEVKITV1_RHS1.VDD_3V3, dht_skt.pin1, r4.Pin_0, oled_skt.pin3, keypad.pin2, r5.Pin_1, r6.Pin_1
  N1: ESPDEVKITV1_RHS1.GPIO15, sounder.pin1
  N2: ESPDEVKITV1_RHS1.GPIO16, co2_sensor.pin1
  N3: ESPDEVKITV1_RHS1.GPIO17, co2_sensor.pin2
  N4: ESPDEVKITV1_RHS1.GPIO21-I2C_SDA, oled_skt.pin1, r5.Pin_0
  N5: ESPDEVKITV1_RHS1.GPIO22-I2C_SCL, oled_skt.pin2, r6.Pin_0
  N6: DHT23.Vcc, J2.pin1
  N7: DHT23.Data-signal, J2.pin2
  N8: DHT23.GND_1, J2.pin3
  5V: ESPDEVKITV1_LHS1.VIN, C3.+, co2_sensor.pin3
  N9: ESPDEVKITV1_LHS1.GPIO13, r1.Pin_0
  N10: ESPDEVKITV1_LHS1.GPIO12, r2.Pin_0
  N11: ESPDEVKITV1_LHS1.GPIO14, r3.Pin_0
  N12: ESPDEVKITV1_LHS1.GPIO25, dht_skt.pin2, r4.Pin_1
  N13: ESPDEVKITV1_LHS1.GPIO39, switch1.pin1
  N14: ESPDEVKITV1_LHS1.GPIO36, keypad.pin1
  N15: green.+ve, r1.Pin_1
  N16: yellow.+ve, r2.Pin_1
  N17: r3.Pin_1, red.+ve
  N18: OLED.GND, OLED_plg.pin4
  N19: OLED.VCC, OLED_plg.pin3
  N20: OLED.SDA, OLED_plg.pin1
  N21: OLED.SCL, OLED_plg.pin2
  N22: J3.pin1, sounder_plg.pin2
  N23: J3.pin2, sounder_plg.pin1
  N24: switch1.pin2, switch2.pin2

notes:
  Note that GPIO_NUM_34 – GPIO_NUM_39 are input mode only
