# Fritzing sketch co2monitor v1.00b (saved by Fritzing 0.9.3b)
stripboards: 1

parts:
  C2 = Electrolytic Capacitor [capacitance=0.1mF package="100 mil [THT, electrolytic]"]
  ESPDEVKITV1_RHS1 = ESP32 DEVKITV1 RHS - 15 pins [form="♀ (female)" package=THT]
  LED3 = smd LED [color="Red (635nm)" package="0603 [SMD]"]  # not connected
  LED4 = smd LED [color="Green (555nm)" package="0603 [SMD]"]  # not connected
  DHT23 = Humidity and Temperature Sensor RHT03
  ESPDEVKITV1_LHS1 = ESP32 DEVKITV1 LHS - 15 pins [form="♀ (female)" package=THT]
  C3 = Electrolytic Capacitor [capacitance=10µF package="100 mil [THT, electrolytic]"]
  RED_LED_Header = LED Female Header [form="♀ (female)" package=THT]
  Green_LED_Header = LED Female Header [form="♀ (female)" package=THT]
  part = female pin header, 5 pins [form="♀ (female)"]
  co2_sensor = female pin header, 4 pins [form="♀ (female)"]
  LED5 = smd LED [color="Yellow (595nm)" package="0603 [SMD]"]  # not connected
  R9 = Resistor [tolerance=±5% resistance=220 package=THT]
  R10 = Resistor [tolerance=±5% resistance=220 package=THT]
  R11 = Resistor [tolerance=±5% resistance=220 package=THT]
  YellowLED_Header1 = LED Female Header [form="♀ (female)" package=THT]
  DHT22_Header = female pin header, 3 pins [form="♀ (female)"]
  J2 = male pin header, 3 pins [form="♂ (male)"]

nets:
  GND: C2.-, ESPDEVKITV1_RHS1.GND, ESPDEVKITV1_LHS1.GND, C3.-, RED_LED_Header.-ve, Green_LED_Header.-ve, co2_sensor.pin2, YellowLED_Header1.-ve, DHT22_Header.pin1
  3.3V: C2.+, ESPDEVKITV1_RHS1.VDD_3V3, DHT22_Header.pin3
  N1: ESPDEVKITV1_RHS1.GPIO16, part.pin3
  N2: ESPDEVKITV1_RHS1.GPIO17, part.pin2
  N3: DHT23.Vcc, J2.pin3
  N4: DHT23.Data-signal, J2.pin2
  N5: DHT23.GND_2, J2.pin1
  5V: ESPDEVKITV1_LHS1.VIN, C3.+, co2_sensor.pin1
  N6: ESPDEVKITV1_LHS1.GPIO13, R9.Pin_0
  N7: ESPDEVKITV1_LHS1.GPIO12, R10.Pin_0
  N8: ESPDEVKITV1_LHS1.GPIO14, R11.Pin_0
  N9: ESPDEVKITV1_LHS1.GPIO25, DHT22_Header.pin2
  N10: RED_LED_Header.+ve, R9.Pin_1
  N11: Green_LED_Header.+ve, R10.Pin_1
  N12: R11.Pin_1, YellowLED_Header1.+ve

notes:
  Note that GPIO_NUM_34 – GPIO_NUM_39 are input mode only
  note orange wire for 5v tx vcc mod
